// Logisim project CSE231(Project- (IPL-2021)) (7 segment display with counter) (logisim).circ as structural Verilog: 1 circuit, main circuit Project
module Project (
  input  in_1,
  output A,
  output B,
  output C
);

  wire and_1_out, and_2_out, and_3_out, and_4_out, and_5_out, and_6_out, and_7_out, and_8_out, and_9_out,
       and_10_out, and_11_out, and_12_out, and_13_out, clock_1_out, j_k_ff_2_qn, j_k_ff_3_qn, not_1_out,
       not_2_out, not_3_out, not_4_out, not_5_out, not_6_out, not_7_out, not_8_out, not_9_out, not_10_out,
       not_11_out, not_12_out, not_13_out, not_14_out, not_15_out, not_16_out, or_1_out, or_2_out, or_3_out,
       or_4_out, or_5_out, or_6_out, or_7_out;

  J_K_Flip_Flop j_k_ff_1 (.J(in_1), .clk(j_k_ff_2_qn), .K(in_1), .Q(A));  // open: Qn, preset, en, reset
  J_K_Flip_Flop j_k_ff_2 (.J(in_1), .clk(j_k_ff_3_qn), .K(in_1), .Q(B), .Qn(j_k_ff_2_qn));  // open: preset, en, reset
  Clock clock_1 (.out(clock_1_out));
  J_K_Flip_Flop j_k_ff_3 (.J(in_1), .clk(clock_1_out), .K(in_1), .Q(C), .Qn(j_k_ff_3_qn));  // open: preset, en, reset
  not not_1 (not_1_out, B);
  not not_2 (not_2_out, C);
  not not_3 (not_3_out, B);
  not not_4 (not_4_out, A);
  not not_5 (not_5_out, B);
  not not_6 (not_6_out, C);
  not not_7 (not_7_out, C);
  not not_8 (not_8_out, B);
  not not_9 (not_9_out, B);
  not not_10 (not_10_out, C);
  not not_11 (not_11_out, B);
  not not_12 (not_12_out, B);
  not not_13 (not_13_out, A);
  not not_14 (not_14_out, C);
  not not_15 (not_15_out, A);
  not not_16 (not_16_out, C);
  and and_1 (and_1_out, not_1_out, C);
  and and_2 (and_2_out, A, not_2_out);
  or or_1 (or_1_out, not_3_out, A);
  and and_3 (and_3_out, not_4_out, not_5_out, not_6_out);
  and and_4 (and_4_out, A, C);
  and and_5 (and_5_out, B, not_7_out);
  and and_6 (and_6_out, A, not_8_out);
  and and_7 (and_7_out, not_9_out, C);
  and and_8 (and_8_out, B, not_10_out);
  and and_9 (and_9_out, A, not_11_out);
  and and_10 (and_10_out, not_12_out, C);
  and and_11 (and_11_out, not_13_out, B, not_14_out);
  and and_12 (and_12_out, not_15_out, C);
  and and_13 (and_13_out, A, not_16_out);
  or or_2 (or_2_out, and_1_out, and_2_out);
  or or_3 (or_3_out, and_3_out, and_4_out);
  or or_4 (or_4_out, and_5_out, and_6_out);
  or or_5 (or_5_out, and_7_out, and_8_out, and_9_out);
  or or_6 (or_6_out, and_10_out, and_11_out);
  or or_7 (or_7_out, and_12_out, and_13_out);
  _7_Segment_Display u_7_segment_display_1 (
    .g(or_7_out), .f(or_6_out), .a(or_2_out), .b(or_1_out), .e(or_5_out), .d(or_4_out), .c(or_3_out));  // open: dp
endmodule
